# Fritzing sketch stm final (saved by Fritzing 0.9.3b)
breadboards: 2

parts:
  J1 = STM32 Nucleo boards
  LED1 = smd LED [color="Red (633nm)" package="0603 [SMD]"]
  LED2 = smd LED [color="Red (633nm)" package="0603 [SMD]"]
  LED3 = smd LED [color="Red (633nm)" package="0603 [SMD]"]
  R1 = Resistor [tolerance=±5% resistance=220 package="1206 [SMD]"]
  R2 = Resistor [tolerance=±5% resistance=220 package="1206 [SMD]"]
  R3 = Resistor [tolerance=±5% resistance=220 package="1206 [SMD]"]
  LCD1 = LCD screen
  U1 = POT [package=pot_alpha_rv16af-20]
  J2 = Piezo Speaker
  S1 = Pushbutton [package="[THT]"]
  R4 = Resistor [tolerance=±5% resistance=220 package="1206 [SMD]"]
  R5 = Photocell (LDR) [package=THT]
  R6 = Resistor [tolerance=±5% resistance=220 package="1206 [SMD]"]
  J3 = Basic Servo

nets:
  N1: J1.A0, U1.S
  N2: J1.A1, R5.pin_0, R6.Pin_1
  N3: J1.D9_PWM, LCD1.DB4
  N4: J1.D10_PWM/SS, LCD1.DB5
  N5: J1.D11_PWM/MOSI, LCD1.DB6
  N6: J1.D12/MISO, LCD1.DB7
  N7: J1.D4, LCD1.RS
  N8: J1.D5_PWM, LCD1.E
  5V: J1.5V, LCD1.VDD, LCD1.LED+, U1.A, S1.Pin_1, S1.Pin_2, R5.pin_1, J3.vcc
  GND: J1.GND, LCD1.VSS, LCD1.R/W, LCD1.LED-, U1.E, J2.pin1, R6.Pin_0, J3.gnd
  N9: J1.PA5, R2.Pin_1
  N10: J1.PA9, J2.pin2, S1.Pin_3, S1.Pin_4, R4.Pin_1
  N11: J1.PA4, R1.Pin_1
  N12: J1.PA15, J3.pulse
  N13: LED1.cathode, LED2.cathode, LED3.cathode
  N14: LED1.anode, R2.Pin_0
  N15: LED2.anode, R1.Pin_0
  N16: LED3.anode, R3.Pin_0
